# Fritzing sketch toggle_button_debounce (saved by Fritzing 1.0.1rc)
breadboards: 1

parts:
  A1 = Arduino UNO R4 WiFi
  S1 = Pushbutton [package="[THT]"]
  R2 = Resistor [tolerance=±5% resistance=1k package="0402 [SMD]"]
  R1 = Resistor [tolerance=±5% resistance=220 package="0402 [SMD]"]
  LED1 = smd LED [color="White (6500K)" package="0805 [SMD]"]

nets:
  N1: A1.Pin_2, A1.Pin_10, A1.Pin_30, A1.Pin_48, R2.Pin_0, LED1.cathode
  N2: A1.Pin_8, S1.Pin_1, S1.Pin_2
  N3: A1.Pin_36, S1.Pin_3, S1.Pin_4, R2.Pin_1
  N4: A1.Pin_46, R1.Pin_1
  N5: R1.Pin_0, LED1.anode

custom parts:
  Arduino UNO R4 WiFi: The Arduino UNO R4 WiFi merges the RA4M1 microprocessor from Renesas with the ESP32-S3 from Espressif, creating an all-in-one tool for makers with enhanced processing power and a diverse array of new peripherals.
